# Fritzing sketch 05-servo (saved by Fritzing 0.9.3b)
breadboards: 1

parts:
  R1 = BBC MicroBit
  BATT1 = 3xAAA Switchable Battery Pack w/JST connector
  J1 = Basic Servo

nets:
  GND: R1.GND, BATT1.NEG, J1.gnd
  N1: R1.P0_ANALOG_IN, J1.pulse
  N2: BATT1.POS, J1.vcc

custom parts:
  BBC MicroBit: The BBC MICRO:BIT
  3xAAA Switchable Battery Pack w/JST connector: 3xAAA Switchable Battery Pack with JST connector
