# Fritzing sketch 06-hc-sr04 (saved by Fritzing 0.9.3b)
breadboards: 1

parts:
  R1 = BBC MicroBit
  BATT1 = 3xAAA Switchable Battery Pack w/JST connector
  hc-sr1 = hc-sr04

nets:
  GND: R1.GND, BATT1.NEG, hc-sr1.GND
  N1: R1.P2_-_ANALOG_IN, hc-sr1.Echo
  N2: R1.P1_ANALOG_IN, hc-sr1.Trig
  N3: BATT1.POS, hc-sr1.VCC

custom parts:
  BBC MicroBit: The BBC MICRO:BIT
  3xAAA Switchable Battery Pack w/JST connector: 3xAAA Switchable Battery Pack with JST connector
